# Fritzing sketch diagram (saved by Fritzing 0.9.10b)
breadboards: 1

parts:
  Q1 = Basic FET P-Channel [package="TO220 [THT]"]
  R1 = Resistor [tolerance=±5% power=0.25 resistance=220 package=THT]
  D1 = Rectifier Diode [part_number=1N4001 package="300 mil [THT]"]
  R2 = Resistor [tolerance=±5% power=0.25 resistance=220 package=THT]
  C1 = Ceramic Capacitor [capacitance=100nF voltage=35V package="100 mil [THT, multilayer]"]
  C2 = Ceramic Capacitor [capacitance=1mF voltage=35V package="100 mil [THT, multilayer]"]
  C3 = Electrolytic Capacitor [capacitance=1µF voltage=35V package="100 mil [THT, electrolytic]"]
  DHT1 = DHT11 Humitidy and Temperature Sensor
  Componente1 = Adafruit TPL5110 Power Timer [part_number="Adafruit #3435"]
  Mod1 = Amica NodeMCU DEVKIT 1.0
  U1 = LIPO-2000mAh [package=lipo-2000]
  Part1 = Solar Panel [package="Renogy 50 Watts 12 Volt Monocrystalline Bendable Solar Panel"]
  Part2 = Solar Panel [package="Renogy 50 Watts 12 Volt Monocrystalline Bendable Solar Panel"]
  Part3 = Solar Charge Controller [part_number="HGX Series Solar Charge Controller PWM" package=PWM-Model]
  U2 = RELAY [package=OJ]

nets:
  GND: Q1.gate, R2.Pin_1, C1.0, C2.0, C3.-, DHT1.GND, Componente1.GND, Mod1.pin_9, Mod1.pin_29, Part3.Connector_6, U2.COIL2
  N1: Q1.drain, U2.NO
  N2: Q1.source, Mod1.pin_30
  N3: R1.Pin_0, C3.+, Mod1.pin_21
  N4: R1.Pin_1, R2.Pin_0, Componente1.DONE
  N5: D1.cathode, C1.1, C2.1, Componente1.VDD
  N6: D1.anode, Part3.Connector_5, U2.MAIN
  N7: DHT1.VDD, Mod1.pin1, Mod1.pin_10, Mod1.pin_26
  N8: DHT1.DATA, Mod1.pin_11
  N9: Componente1.PWROUT, U2.COIL1
  N10: U1.+, Part3.Connector_3
  N11: U1.-, Part3.Connector_4
  N12: Part1.Connector_1, Part2.Connector_1, Part3.Connector_1
  N13: Part1.Connector_2, Part2.Connector_2, Part3.Connector_2

notes:
  Panel solar 6W
  Bateria Litio 1300mAh
  MH CD42
  MOSFET-P
  Rele Opto
  ESP32
  TPL5110
  R10KOhm
  R4.7KOhm
  C100nF
  Diodo
  C1F
  DHT11

custom parts:
  DHT11 Humitidy and Temperature Sensor: DHT11 Humidity and Temperature Sensor
  Adafruit TPL5110 Power Timer: With some development boards, low power usage is an afterthought. Especially when price and usability is the main selling point. So what should you do when its time to turn around and make that project of yours run on a battery or solar? Sure you could try to hot-air that regulator off, or you could jerry-rig a relay. Or, use a 555? Ugh, the options aren't that great. The Adafruit TPL5110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
  Solar Panel: Renogy 50 Watts 12 Volt Solar Panel
  Solar Charge Controller: PWM-Solar Charge Controller
